# Fritzing sketch smarthack (saved by Fritzing 0.9.2b)

parts:
  Part1 = LSM9DS0 9DOF Accel/Mag/Gyro+Temp
  Part2 = HUZZAH ESP8266 Breakout
  U2 = SWITCH_SPDT [package=kps-1290]
  Power_plug1 = Power plug
  U1 = LIPO-110mAh [package=lipo-110]

nets:
  N1: Part1.SDA_5V, Part2.GPIO4
  N2: Part1.SCL_5V, Part2.GPIO5
  GND: Part1.GND, Part2.GND, Power_plug1.GND, U1.-
  VIN: Part1.VIN, Part2.3.3V
  VIN_2: Part2.VIN, Power_plug1.VCC
  N3: Part2.VBAT, U2.S
  N4: U2.P, U1.+

custom parts:
  LSM9DS0 9DOF Accel/Mag/Gyro+Temp: Add motion, direction and orientation sensing to your Arduino project with this all-in-one 9-DOF sensor. Inside the chip are three sensors, one is a classic 3-axis accelerometer, which can tell you which direction is down towards the Earth (by measuring gravity) or how fast the board is accelerating in 3D space. The other is a 3-axis magnetometer that can sense where the strongest magnetic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
  HUZZAH ESP8266 Breakout: The ESP8266 processor from Espressif is an 80 MHz microcontroller with a full WiFi front-end (both as client and access point) and TCP/IP stack with DNS support as well.
